// Logisim project Lab5-1.circ as structural Verilog: 3 circuits, main circuit main
module main (
  input  [3:0] a,
  input  [3:0] b,
  input  [1:0] in_3
);

  wire [3:0] multiplexer_1_out, multiplier_1_out, n4_bit_adder_1_out_3, shifter_1_out, subtractor_1_out;

  _4_bit_adder u_4_bit_adder_1 (.in_1(a), .in_2(b), .out_3(n4_bit_adder_1_out_3));
  Subtractor #(.width(4)) subtractor_1 (.a(a), .b(b), .out(subtractor_1_out));  // open: bin, bout
  Multiplier #(.width(4)) multiplier_1 (.a(a), .b(b), .out(multiplier_1_out));  // open: cin, cout
  Shifter #(.width(4), .shift("ar")) shifter_1 (.in(a), .\dist (b[3:2]), .out(shifter_1_out));
  // Probe on n4_bit_adder_1_out_3
  // Probe on subtractor_1_out
  // Probe on multiplier_1_out
  // Probe on shifter_1_out
  // Probe on multiplexer_1_out
  Multiplexer #(.select(2), .width(4)) multiplexer_1 (
    .in0(n4_bit_adder_1_out_3), .in1(subtractor_1_out), .in2(multiplier_1_out), .in3(shifter_1_out),
    .out(multiplexer_1_out), .sel(in_3));  // open: en
endmodule

module _4_bit_adder (
  input  [3:0] in_1,
  input  [3:0] in_2,
  output [3:0] out_3
);

  wire my_1_bit_adder_1_cout, my_1_bit_adder_2_cout, my_1_bit_adder_3_cout;

  my_1_bit_adder my_1_bit_adder_1 (.A(in_1[0]), .B(in_2[0]), .Cin(1'b0), .Cout(my_1_bit_adder_1_cout), .S(out_3[0]));
  my_1_bit_adder my_1_bit_adder_2 (
    .A(in_1[1]), .B(in_2[1]), .Cin(my_1_bit_adder_1_cout), .Cout(my_1_bit_adder_2_cout), .S(out_3[1]));
  my_1_bit_adder my_1_bit_adder_3 (
    .A(in_1[2]), .B(in_2[2]), .Cin(my_1_bit_adder_2_cout), .Cout(my_1_bit_adder_3_cout), .S(out_3[2]));
  my_1_bit_adder my_1_bit_adder_4 (.A(in_1[3]), .B(in_2[3]), .Cin(my_1_bit_adder_3_cout), .S(out_3[3]));  // open: Cout
endmodule

module my_1_bit_adder (
  input  A,
  input  B,
  input  Cin,
  output Cout,
  output S
);

  wire and_1_out, and_2_out, and_3_out, and_4_out, and_5_out, and_6_out, and_7_out, not_1_out, not_2_out,
       not_3_out, not_4_out, not_5_out, not_6_out;

  and and_1 (and_1_out, B, Cin);
  and and_2 (and_2_out, A, Cin);
  and and_3 (and_3_out, A, B);
  not not_1 (not_1_out, A);
  not not_2 (not_2_out, B);
  not not_3 (not_3_out, A);
  not not_4 (not_4_out, Cin);
  not not_5 (not_5_out, B);
  not not_6 (not_6_out, Cin);
  or or_1 (Cout, and_1_out, and_2_out, and_3_out);
  and and_4 (and_4_out, not_1_out, not_2_out, Cin);
  and and_5 (and_5_out, not_3_out, B, not_4_out);
  and and_6 (and_6_out, A, not_5_out, not_6_out);
  and and_7 (and_7_out, A, B, Cin);
  or or_2 (S, and_4_out, and_5_out, and_6_out, and_7_out);
endmodule
