// Logisim project Lab5.circ as structural Verilog: 1 circuit, main circuit main
module main (
  input  [3:0] a,
  input  [3:0] b,
  input  [1:0] in_3
);

  wire [3:0] adder_1_out, multiplexer_1_out, multiplier_1_out, shifter_1_out, subtractor_1_out;

  Adder #(.width(4)) adder_1 (.a(a), .b(b), .out(adder_1_out));  // open: cin, cout
  Subtractor #(.width(4)) subtractor_1 (.a(a), .b(b), .out(subtractor_1_out));  // open: bin, bout
  Multiplier #(.width(4)) multiplier_1 (.a(a), .b(b), .out(multiplier_1_out));  // open: cin, cout
  Shifter #(.width(4), .shift("ar")) shifter_1 (.in(a), .\dist (b[3:2]), .out(shifter_1_out));
  // Probe on adder_1_out
  // Probe on subtractor_1_out
  // Probe on multiplier_1_out
  // Probe on shifter_1_out
  // Probe on multiplexer_1_out
  Multiplexer #(.select(2), .width(4)) multiplexer_1 (
    .in0(adder_1_out), .in1(subtractor_1_out), .in2(multiplier_1_out), .in3(shifter_1_out),
    .out(multiplexer_1_out), .sel(in_3));  // open: en
endmodule
