// Logisim project Proj3'.circ as structural Verilog: 4 circuits, main circuit main
module main (
  input  R0_read_en,
  input  R1_read_en,
  input  R2_read_en,
  input  R3_read_en,
  input  decoder_en,
  input  [7:0] in_6,
  output ZERO
);

  wire clock_1_out, control_1_dis, control_1_halt, control_1_ld, control_1_m_rt, control_1_out_4,
       control_1_pc_imm, control_1_rd_2, control_1_rt_2, control_1_sd, control_1_w_b, or_1_out, write_en_out;
  wire [3:0] control_1__0_3, control_1__4_7, rom_1_data_2, undriven, undriven_2;
  wire [7:0] adder_1_out, adder_2_out, alu_1_out_7, control_1_mem_add, control_1_pc, control_1_rd,
       control_1_rt, multiplexer_1_out, multiplexer_2_out, multiplexer_3_out, multiplexer_4_out,
       multiplexer_5_out, pc_q, ram_1_data, reg_1_rs, reg_1_rt, shifter_1_out;
  wire [11:0] rom_1_data;

  Multiplexer #(.width(8)) multiplexer_1 (
    .in0(control_1_pc), .in1(multiplexer_2_out), .out(multiplexer_1_out), .sel(control_1_pc_imm));  // open: en
  Register pc (.D(multiplexer_1_out), .Q(pc_q), .clk(clock_1_out));  // open: en, clr
  Clock #(.highDuration(2), .lowDuration(2)) clock_1 (.out(clock_1_out));
  Adder adder_1 (.a(pc_q), .b(8'h2), .out(adder_1_out));  // open: cin, cout
  Adder adder_2 (
    .a(adder_1_out), .b({rom_1_data[1:0], rom_1_data[3:2], rom_1_data[5:4], rom_1_data[7:6]}),
    .out(adder_2_out));  // open: cin, cout
  Shifter shifter_1 (.in(adder_2_out), .\dist (3'b001), .out(shifter_1_out));
  ROM #(.dataWidth(16)) rom_1 (.addr(pc_q), .data({rom_1_data_2, rom_1_data}), .sel(control_1_halt));
  Multiplexer #(.width(8)) multiplexer_2 (
    .in0(adder_1_out), .in1(shifter_1_out), .out(multiplexer_2_out), .sel(control_1_out_4));  // open: en
  Multiplexer #(.width(8)) multiplexer_3 (
    .in0(control_1_rd), .in1(control_1_rt), .out(multiplexer_3_out), .sel(control_1_rt_2));  // open: en
  Clock write_en (.out(write_en_out));
  Multiplexer #(.width(8)) multiplexer_4 (
    .in0(multiplexer_3_out), .in1(ram_1_data), .out(multiplexer_4_out), .sel(control_1_m_rt));  // open: en
  RAM ram_1 (.addr(control_1_mem_add), .data(ram_1_data), .clk(control_1_sd), .ld(control_1_ld));  // open: sel, clr
  Multiplexer #(.width(8)) multiplexer_5 (
    .in0(in_6), .in1(multiplexer_4_out), .out(multiplexer_5_out), .sel(control_1_w_b));  // open: en
  REG reg_1 (
    .in_1(write_en_out), .in_2(R0_read_en), .in_3(R1_read_en), .in_4(R2_read_en), .in_5(R3_read_en),
    .in_7(rom_1_data[11:10]), .in_6(decoder_en), .in_9(rom_1_data[9:8]), .in_11(rom_1_data[7:6]),
    .in_12(multiplexer_5_out), .RS(reg_1_rs), .RT(reg_1_rt), .in_8(or_1_out), .in_10(control_1_rd_2));
  or or_1 (or_1_out, control_1_rt_2, control_1_m_rt);
  ALU alu_1 (
    .RS(reg_1_rs), .RT(reg_1_rt), .IM({rom_1_data[1:0], rom_1_data[3:2], rom_1_data[5:4], rom_1_data[7:6]}),
    .Zero(ZERO), ._2_3(rom_1_data_2[3:2]), ._0_1(rom_1_data_2[1:0]), .out_7(alu_1_out_7));
  control control_1 (
    .in_1(alu_1_out_7), .RD(control_1_rd), .out_4(control_1_out_4), .PC(control_1_pc), .RT(control_1_rt),
    ._0_3(control_1__0_3), ._4_7(control_1__4_7), .mem_add(control_1_mem_add), .in_2(rom_1_data_2),
    .HALT(control_1_halt), .dis(control_1_dis), .ld(control_1_ld), .pc_imm(control_1_pc_imm),
    .sd(control_1_sd), .w_b(control_1_w_b), .M_RT(control_1_m_rt), .RT_2(control_1_rt_2),
    .RD_2(control_1_rd_2));
  Transistor #(.\type ("n"), .width(4)) transistor_1 (.in(undriven), .out(control_1__4_7), .gate(control_1_dis));
  Transistor #(.\type ("n"), .width(4)) transistor_2 (.in(undriven_2), .out(control_1__0_3), .gate(control_1_dis));
  Hex_Digit_Display hex_digit_display_1 (.value(undriven));  // open: dp
  Hex_Digit_Display hex_digit_display_2 (.value(undriven_2));  // open: dp

  // Notes on the sheet:
  //   contents of rom_1 (hex, n*v repeats v):
  //   1 11 13*0 1 0 10
  //   RT
endmodule

module ALU (
  input  [7:0] RS,
  input  [7:0] RT,
  input  [7:0] IM,
  input  [1:0] _2_3,
  input  [1:0] _0_1,
  output Zero,
  output [7:0] out_7
);

  wire comparator_1_eq, comparator_1_lt;
  wire [7:0] adder_1_out, adder_2_out, bit_extender_1_out, bit_extender_2_out, divider_1_rem, random_1_out,
       subtractor_1_out, xor_1_out;

  Comparator comparator_1 (.a(RS), .b(RT), .eq(comparator_1_eq), .lt(comparator_1_lt));  // open: gt
  Random random_1 (.out(random_1_out));  // open: clk, next, clr
  Divider divider_1 (.a(random_1_out), .b(RS), .rem(divider_1_rem));  // open: out, upper
  Adder adder_1 (.a(RS), .b(RT), .out(adder_1_out));  // open: cin, cout
  Subtractor subtractor_1 (.a(RS), .b(RT), .out(subtractor_1_out));  // open: bin, bout
  assign bit_extender_1_out = {{7{1'b0}}, comparator_1_lt};  // Bit_Extender bit_extender_1
  assign xor_1_out = RS ^ RT;  // XOR_Gate xor_1, 8 bits wide
  Adder adder_2 (.a(RS), .b(IM), .out(adder_2_out));  // open: cin, cout
  assign bit_extender_2_out = {{7{1'b0}}, comparator_1_eq};  // Bit_Extender bit_extender_2
  nand nand_1 (Zero, out_7[7], out_7[6], out_7[5], out_7[4], out_7[3], out_7[2], out_7[1], out_7[0]);
  Multiplexer #(.select(4), .width(8)) multiplexer_1 (
    .in0(adder_1_out), .in1(subtractor_1_out), .in2(bit_extender_1_out), .in4(adder_2_out),
    .in5(bit_extender_2_out), .in6(xor_1_out), .in8(adder_2_out), .in9(IM), .in13(divider_1_rem), .in14(RS),
    .out(out_7), .sel({_2_3, _0_1}));  // open: in3, in7, in10, in11, in12, in15, en
endmodule

module REG (
  input  in_1,
  input  in_2,
  input  in_3,
  input  in_4,
  input  in_5,
  input  in_6,
  input  [1:0] in_7,
  input  in_8,
  input  [1:0] in_9,
  input  in_10,
  input  [1:0] in_11,
  input  [7:0] in_12,
  output [7:0] RS,
  output [7:0] RT
);

  wire and_1_out, and_2_out, and_3_out, and_4_out, decoder_1_out0, decoder_1_out1, decoder_1_out2,
       decoder_1_out3;
  wire [7:0] R0_q, R1_q, R2_q, R3_q;

  Decoder #(.select(2), .tristate("true")) decoder_1 (
    .out0(decoder_1_out0), .out1(decoder_1_out1), .out2(decoder_1_out2), .out3(decoder_1_out3), .sel(in_7),
    .en(in_6));
  Decoder #(.select(2), .tristate("true")) decoder_2 (
    .out0(decoder_1_out0), .out1(decoder_1_out1), .out2(decoder_1_out2), .out3(decoder_1_out3), .sel(in_9),
    .en(in_8));
  Decoder #(.select(2), .tristate("true")) decoder_3 (
    .out0(decoder_1_out0), .out1(decoder_1_out1), .out2(decoder_1_out2), .out3(decoder_1_out3), .sel(in_11),
    .en(in_10));
  and and_1 (and_1_out, in_1, decoder_1_out0);
  and and_2 (and_2_out, in_1, decoder_1_out1);
  and and_3 (and_3_out, in_1, decoder_1_out2);
  and and_4 (and_4_out, in_1, decoder_1_out3);
  Register R0 (.D(in_12), .en(in_2), .Q(R0_q), .clk(and_1_out));  // open: clr
  Register R1 (.D(in_12), .en(in_3), .Q(R1_q), .clk(and_2_out));  // open: clr
  Register R2 (.D(in_12), .en(in_4), .Q(R2_q), .clk(and_3_out));  // open: clr
  Register R3 (.D(in_12), .en(in_5), .Q(R3_q), .clk(and_4_out));  // open: clr
  Multiplexer #(.select(2), .width(8)) multiplexer_1 (
    .in0(R0_q), .in1(R1_q), .in2(R2_q), .in3(R3_q), .out(RS), .sel(in_7));  // open: en
  Multiplexer #(.select(2), .width(8)) multiplexer_2 (
    .in0(R0_q), .in1(R1_q), .in2(R2_q), .in3(R3_q), .out(RT), .sel(in_9));  // open: en
endmodule

module control (
  input  [7:0] in_1,
  input  [3:0] in_2,
  output [7:0] RD,
  output out_4,
  output [7:0] PC,
  output [7:0] mem_add,
  output [7:0] RT,
  output [3:0] _0_3,
  output [3:0] _4_7,
  output RD_2,
  output w_b,
  output sd,
  output pc_imm,
  output RT_2,
  output ld,
  output M_RT,
  output dis,
  output HALT
);

  wire decoder_1_out0, decoder_1_out1, decoder_1_out2, decoder_1_out4, decoder_1_out7, decoder_1_out13,
       decoder_1_out15;
  wire [7:0] demultiplexer_1_out0, demultiplexer_1_out1, demultiplexer_1_out2, demultiplexer_1_out5,
       demultiplexer_1_out7;

  Demultiplexer #(.select(4), .width(8)) demultiplexer_1 (
    .out0(demultiplexer_1_out0), .out1(demultiplexer_1_out1), .out2(demultiplexer_1_out2), .out4(RT),
    .out5(demultiplexer_1_out5), .out7(demultiplexer_1_out7), .out8(mem_add), .out9(PC), .out12(mem_add),
    .out13(RT), .out14({_4_7, _0_3}), .in(in_1), .sel(in_2));  // open: out3, out6, out10, out11, out15, en
  Decoder #(.select(4)) decoder_1 (
    .out0(decoder_1_out0), .out1(decoder_1_out1), .out2(decoder_1_out2), .out4(decoder_1_out4),
    .out7(decoder_1_out7), .out8(sd), .out9(pc_imm), .out12(ld), .out13(decoder_1_out13), .out14(dis),
    .out15(decoder_1_out15), .sel(in_2));  // open: out3, out5, out6, out10, out11, en
  not not_1 (HALT, decoder_1_out15);
  Bit_Extender #(.out_width(1)) bit_extender_1 (.in(demultiplexer_1_out5), .out(out_4));
  assign RD = demultiplexer_1_out0 | demultiplexer_1_out1 | demultiplexer_1_out2 | demultiplexer_1_out7;  // OR_Gate or_1, 8 bits wide
  or or_2 (M_RT, ld, sd);
  or or_3 (w_b, decoder_1_out0, decoder_1_out1, decoder_1_out2, decoder_1_out4, decoder_1_out7, decoder_1_out13);
  or or_4 (RT_2, decoder_1_out4, decoder_1_out13);
  or or_5 (RD_2, decoder_1_out7, decoder_1_out0, decoder_1_out1, decoder_1_out2);
endmodule
