// Logisim project wentao_2.circ as structural Verilog: 2 circuits, main circuit main
module main (
  input  in_1,
  input  in_2,
  input  [7:0] in_3,
  input  write_en,
  input  R0_read_en,
  input  [7:0] in_6,
  input  R1_read_en,
  input  R2_read_en,
  input  R3_read_en,
  input  in_10,
  input  decoder_en,
  input  [7:0] in_12
);

  wire clock_1_out, comparator_1_lt;
  wire [3:0] rom_1_data_2;
  wire [7:0] adder_1_out, adder_2_out, adder_3_out, adder_4_out, adder_5_out, bit_extender_1_out,
       multiplexer_1_out, multiplexer_2_out, register_1_q, register_file_1_out_9, register_file_2_out_9,
       rom_2_data, subtractor_1_out, undriven, xor_1_out;
  wire [15:4] rom_1_data;

  Clock #(.highDuration(21), .lowDuration(21)) clock_1 (.out(clock_1_out));
  Register register_1 (.D(adder_2_out), .Q(register_1_q), .clk(clock_1_out), .clr(in_2));  // open: en
  Clock clock_2 ();  // open: out
  Multiplexer #(.width(8)) multiplexer_1 (
    .in0(register_1_q), .in1(adder_3_out), .out(multiplexer_1_out), .sel(in_1));  // open: en
  Adder adder_1 (.a(adder_1_out), .b(in_6), .out(adder_1_out));  // open: cin, cout
  Adder adder_2 (.a(multiplexer_1_out), .b(in_3), .out(adder_2_out));  // open: cin, cout
  ROM #(.dataWidth(16)) rom_1 (
    .addr(multiplexer_1_out), .data({rom_1_data, rom_1_data_2[1:0], rom_1_data_2[3:2]}));  // open: sel
  ROM #(.dataWidth(16)) rom_2 (
    .addr(adder_1_out),
    .data({rom_1_data_2[1:0], rom_1_data_2[3:2], rom_1_data[5:4], rom_1_data[7:6], rom_2_data}), .sel(in_10));
  Adder adder_3 (.a(multiplexer_1_out), .b(rom_1_data[15:8]), .out(adder_3_out));  // open: cin, cout
  RAM ram_1 ();  // open: addr, data, sel, clk, ld, clr
  // Probe on register_file_1_out_9
  register_file register_file_1 (
    .in_1(write_en), .in_2(R0_read_en), .in_3(R1_read_en), .in_4(R2_read_en), .in_5(R3_read_en),
    .in_6(rom_1_data[5:4]), .in_8(in_12), .out_9(register_file_1_out_9), .in_7(decoder_en));
  register_file register_file_2 (
    .in_1(write_en), .in_2(R0_read_en), .in_3(R1_read_en), .in_4(R2_read_en), .in_5(R3_read_en),
    .in_6(rom_1_data[7:6]), .in_8(in_12), .out_9(register_file_2_out_9), .in_7(decoder_en));
  register_file register_file_3 (
    .in_1(write_en), .in_2(R0_read_en), .in_3(R1_read_en), .in_4(R2_read_en), .in_5(R3_read_en),
    .in_6(rom_2_data[7:6]), .in_7(decoder_en));  // open: in_8, out_9
  Comparator comparator_1 (.a(register_file_1_out_9), .b(register_file_2_out_9), .lt(comparator_1_lt));  // open: gt, eq
  Hex_Digit_Display hex_digit_display_1 (.value(undriven[7:4]));  // open: dp
  Hex_Digit_Display hex_digit_display_2 (.value(undriven[3:0]));  // open: dp
  Adder adder_4 (.a(register_file_1_out_9), .b(register_file_2_out_9), .out(adder_4_out));  // open: cin, cout
  Subtractor subtractor_1 (
    .a(register_file_1_out_9), .b(register_file_2_out_9), .out(subtractor_1_out));  // open: bin, bout
  assign bit_extender_1_out = {{7{1'b0}}, comparator_1_lt};  // Bit_Extender bit_extender_1
  Adder adder_5 (.a(register_file_1_out_9), .b(rom_1_data[15:8]), .out(adder_5_out));  // open: cin, cout
  assign xor_1_out = register_file_1_out_9 ^ register_file_2_out_9;  // XOR_Gate xor_1, 8 bits wide
  Hex_Digit_Display hex_digit_display_3 (.value(adder_4_out[7:4]));  // open: dp
  Hex_Digit_Display hex_digit_display_4 (.value(subtractor_1_out[7:4]));  // open: dp
  Hex_Digit_Display hex_digit_display_5 (.value(adder_4_out[3:0]));  // open: dp
  Hex_Digit_Display hex_digit_display_6 (.value(subtractor_1_out[3:0]));  // open: dp
  Multiplexer #(.select(4), .width(8)) multiplexer_2 (
    .in0(adder_4_out), .in1(subtractor_1_out), .in2(bit_extender_1_out), .in6(xor_1_out),
    .out(multiplexer_2_out), .sel(rom_1_data_2));  // open: in3, in4, in5, in7, in8, in9, in10, in11, in12, in13, in14, in15, en

  // Notes on the sheet:
  //   contents of rom_1 (hex, n*v repeats v):
  //   1 11 13*0 1 0 10
endmodule

module register_file (
  input  in_1,
  input  in_2,
  input  in_3,
  input  in_4,
  input  in_5,
  input  [1:0] in_6,
  input  in_7,
  input  [7:0] in_8,
  output [7:0] out_9
);

  wire and_1_out, and_2_out, and_3_out, and_4_out, decoder_1_out0, decoder_1_out1, decoder_1_out2,
       decoder_1_out3;
  wire [7:0] R0_q, R1_q, R2_q, R3_q;

  Decoder #(.select(2), .tristate("true")) decoder_1 (
    .out0(decoder_1_out0), .out1(decoder_1_out1), .out2(decoder_1_out2), .out3(decoder_1_out3), .sel(in_6),
    .en(in_7));
  Register R0 (.D(in_8), .en(in_2), .Q(R0_q), .clk(and_1_out));  // open: clr
  and and_1 (and_1_out, in_1, decoder_1_out0);
  and and_2 (and_2_out, in_1, decoder_1_out1);
  and and_3 (and_3_out, in_1, decoder_1_out2);
  and and_4 (and_4_out, in_1, decoder_1_out3);
  Register R1 (.D(in_8), .en(in_3), .Q(R1_q), .clk(and_2_out));  // open: clr
  Register R2 (.D(in_8), .en(in_4), .Q(R2_q), .clk(and_3_out));  // open: clr
  Register R3 (.D(in_8), .en(in_5), .Q(R3_q), .clk(and_4_out));  // open: clr
  Multiplexer #(.select(2), .width(8)) multiplexer_1 (
    .in0(R0_q), .in1(R1_q), .in2(R2_q), .in3(R3_q), .out(out_9), .sel(in_6));  // open: en
endmodule
